# Fritzing sketch D1MINI_PC_CONTROL (saved by Fritzing 0.9.4)
circuit board: 5.06689cm x 6.61425cm
breadboards: 1

parts:
  WeMos_D1_Mini = WeMos D1 Mini
  20k = Resistor [tolerance=±5% resistance=20k package=THT]
  100uF = Capacitor Polarized [package=cpol-radial-10uf-25v]
  20k_2 = Resistor [tolerance=±5% resistance=20k package=THT]
  PWR_LED = female pin header, 2 pins [form="♀ (female)"]
  RST_SW = female pin header, 2 pins [form="♀ (female)"]
  PWR_SW = female pin header, 2 pins [form="♀ (female)"]
  PWR_SW_2 = female pin header, 2 pins [form="♀ (female)"]
  RST_SW_2 = female pin header, 2 pins [form="♀ (female)"]
  PWR_LED_2 = female pin header, 2 pins [form="♀ (female)"]
  20k_3 = Resistor [tolerance=±5% resistance=20k package=THT]

nets:
  3.3V: WeMos_D1_Mini.3V3, 100uF.+
  N1: WeMos_D1_Mini.D0, 20k_2.Pin_0, PWR_LED.pin1, PWR_LED_2.pin1
  RST_SW: WeMos_D1_Mini.D6, 20k.Pin_0, RST_SW.pin1, RST_SW_2.pin1
  PWR_SW: WeMos_D1_Mini.D7, PWR_SW.pin1, PWR_SW_2.pin1, 20k_3.Pin_0
  GND: WeMos_D1_Mini.G, 20k.Pin_1, 100uF.-, 20k_2.Pin_1, PWR_LED.pin2, RST_SW.pin2, PWR_SW.pin2, PWR_SW_2.pin2, RST_SW_2.pin2, PWR_LED_2.pin2, 20k_3.Pin_1
